// Logisim project Offline-01.circ as structural Verilog: 1 circuit, main circuit main
module main (
  input  A3,
  input  A2,
  input  A1,
  input  A0,
  input  B3,
  input  B2,
  input  B1,
  input  B0,
  input  CS2,
  input  CS1,
  input  CS0,
  output F3,
  output F2,
  output F1,
  output F0,
  output S,
  output Z,
  output V,
  output C
);

  wire n7404_1_p2, n7404_1_p4, n7404_1_p6, n7404_1_p10, n7404_2_p2, n7404_2_p4, n7404_2_p6, n7404_2_p10,
       n7404_2_p11, n7408_1_p3, n7408_1_p6, n7408_1_p11, n7408_1_p14, n7408_2_p1, n7408_2_p3, n7408_2_p8,
       n7432_1_p3, n7432_1_p6, n7432_1_p11, n7432_1_p14, n7432_2_p3, n7432_2_p6, n7432_2_p11, n7483_1_p8,
       n74153_1_p7, n74153_2_p8, n74153_2_p10, n74153_2_p18, n74157_1_p4, n74157_1_p7, n74157_1_p13,
       n74157_1_p16;

  // _7408 7408_1: pin names not known; wires that end beside it: A3, B3, n7408_1_p3, A2, B2, n7408_1_p6, 1'b0, 1'b1, A1, B1, n7408_1_p11, A0, B0, n7408_1_p14
  // _7408 7408_2: pin names not known; wires that end beside it: n7408_2_p1, CS0, n7408_2_p3, 1'b0, 1'b1, CS2, CS1, n7408_2_p8
  // _7404 7404_1: pin names not known; wires that end beside it: A3, n7404_1_p2, A2, n7404_1_p4, A1, n7404_1_p6, 1'b0, 1'b1, A0, n7404_1_p10, CS1, n7408_2_p1
  // _7432 7432_1: pin names not known; wires that end beside it: A3, B3, n7432_1_p3, A2, B2, n7432_1_p6, 1'b0, 1'b1, A1, B1, n7432_1_p11, A0, B0, n7432_1_p14
  // _7404 7404_2: pin names not known; wires that end beside it: B3, n7404_2_p2, B2, n7404_2_p4, B1, n7404_2_p6, 1'b0, 1'b1, B0, n7404_2_p10, n7404_2_p11, Z
  // _7432 7432_2: pin names not known; wires that end beside it: n7408_2_p3, CS2, n7432_2_p3, F0, F1, n7432_2_p6, 1'b0, 1'b1, n7432_2_p6, F2, n7432_2_p11, n7432_2_p11, F3, n7404_2_p11
  // _74153 74153_1: pin names not known; wires that end beside it: 1'b0, CS2, n7432_1_p3, n7404_1_p2, n7408_1_p3, A3, n74153_1_p7, 1'b1, 1'b0, n7408_2_p3, n7432_1_p6, n7404_1_p4, n7408_1_p6, A2
  // _74153 74153_2: pin names not known; wires that end beside it: 1'b0, 1'b0, CS2, n7432_1_p11, n7404_1_p6, n7408_1_p11, A1, n74153_2_p8, 1'b0, n74153_2_p10, 1'b1, 1'b0, n7408_2_p3, n7432_1_p14, n7404_1_p10, n7408_1_p14, A0, n74153_2_p18
  // _74157 74157_1: pin names not known; wires that end beside it: CS1, B3, n7404_2_p2, n74157_1_p4, B2, n7404_2_p4, n74157_1_p7, 1'b0, 1'b1, n7432_2_p3, B1, n7404_2_p6, n74157_1_p13, B0, n7404_2_p10, n74157_1_p16
  // _7483 7483_1: pin names not known; wires that end beside it: 1'b0, 1'b0, 1'b0, 1'b1, C, 1'b0, 1'b0, n7483_1_p8, 1'b0, n74157_1_p4, n74153_1_p7
  // _7483 7483_2: pin names not known; wires that end beside it: 1'b0, 1'b0, F2, n74153_2_p10, n74157_1_p7, 1'b1, F1, n74157_1_p13, n74153_2_p8, F3, 1'b0, n7483_1_p8, n7408_2_p8, 1'b0, n74157_1_p16, n74153_2_p18, F0
  // _7486 7486_1: pin names not known; wires that end beside it: n7483_1_p8, C, V, 1'b0, 1'b1

  assign S = F3;
endmodule
